// Logisim project Processor_full.circ as structural Verilog: 4 circuits, main circuit main
module main (
);

  wire ALUEnable, ALUOp, and_1_out, CF, Clock, comparator_1_eq, comparator_1_lt, compare, DataEnable,
       demultiplexer_8_out1, demultiplexer_9_out1, ImmEnable, jumpActivate, jumpControl, PCload, PCread,
       PCselect, regLoad, regStore, writeEnable, writeFlag, ZF;
  wire [3:0] multiplexer_5_out, multiplexer_6_out, opcode, Reg1, Reg2, RegSource, state;
  wire [11:0] adder_2_out, bit_extender_2_out, demultiplexer_1_out1, jump, JumpPC, multiplexer_1_out,
       multiplexer_2_out, multiplexer_3_out, multiplexer_4_out, PCValue;
  wire [15:0] alu_1_result_of_operation, bit_extender_1_out, demultiplexer_2_out0, demultiplexer_2_out1,
       demultiplexer_3_out0, demultiplexer_3_out1, demultiplexer_4_out0, demultiplexer_4_out1,
       demultiplexer_5_out0, demultiplexer_6_out1, demultiplexer_7_out1, demultiplexer_10_out1,
       multiplexer_7_out, multiplexer_8_out, ram_1_data, register_file_1_register_1_data,
       register_file_1_register_2_data, TempReg_q;

  Multiplexer #(.width(12), .enable("false")) multiplexer_1 (
    .in0({12{1'b0}}), .in1(demultiplexer_1_out1), .out(multiplexer_1_out), .sel(jumpControl));
  Multiplexer #(.width(12), .enable("false")) multiplexer_2 (
    .in0(multiplexer_4_out), .in1(jump), .out(multiplexer_2_out), .sel(and_1_out));
  and and_1 (and_1_out, jumpActivate, PCload);
  Register #(.width(12)) PC (.D(multiplexer_2_out), .en(PCload), .Q(PCValue), .clk(Clock));  // open: clr
  Adder #(.width(12)) adder_1 (.a(PCValue), .b(multiplexer_1_out), .out(JumpPC));  // open: cin, cout
  Demultiplexer #(.width(12), .enable("false")) demultiplexer_1 (
    .out1(demultiplexer_1_out1), .in({RegSource, Reg1, Reg2}), .sel(PCselect));  // open: out0
  Multiplexer #(.width(12), .enable("false")) multiplexer_3 (
    .in0(PCValue), .in1(PCValue), .out(multiplexer_3_out), .sel(PCread));
  Register #(.width(12)) PC_2 (.D(JumpPC), .en(jumpControl), .Q(jump), .clk(Clock));  // open: clr
  Multiplexer #(.width(12), .enable("false")) multiplexer_4 (
    .in0(adder_2_out), .in1(JumpPC), .out(multiplexer_4_out), .sel(PCselect));
  Adder #(.width(12)) adder_2 (.a(12'h1), .b(PCValue), .out(adder_2_out));  // open: cin, cout
  ROM #(.addrWidth(12), .dataWidth(16)) rom_1 (
    .addr(multiplexer_3_out), .data({opcode, RegSource, Reg1, Reg2}), .sel(1'b1));
  assign bit_extender_1_out = {{12{Reg2[3]}}, Reg2};  // Bit_Extender bit_extender_1
  Multiplexer #(.width(4), .enable("false")) multiplexer_5 (
    .in0(Reg1), .in1(RegSource), .out(multiplexer_5_out), .sel(regStore));
  Multiplexer #(.width(4), .enable("false")) multiplexer_6 (
    .in0(Reg2), .in1(Reg1), .out(multiplexer_6_out), .sel(compare));
  Register_File register_file_1 (
    .write_data(multiplexer_8_out), .register_1_data(register_file_1_register_1_data),
    .register_2_data(register_file_1_register_2_data), .write_source__register(RegSource),
    .write_enable(writeEnable), .Clock(Clock), .read_register1(multiplexer_5_out),
    .read_register_2(multiplexer_6_out));
  Clock clock_1 (.out(Clock));
  Demultiplexer #(.width(16), .enable("false")) demultiplexer_2 (
    .out0(demultiplexer_2_out0), .out1(demultiplexer_2_out1), .in(register_file_1_register_2_data),
    .sel(compare));
  Demultiplexer #(.width(16), .enable("false")) demultiplexer_3 (
    .out0(demultiplexer_3_out0), .out1(demultiplexer_3_out1), .in(register_file_1_register_1_data),
    .sel(compare));
  Control_Unit control_unit_1 (
    .opcode(opcode), .PCRead(PCread), .compare(compare), .ImmEnable(ImmEnable), .regStore(regStore),
    .DataEnable(DataEnable), .writeFlag(writeFlag), .PCSelect(PCselect), .writeEnable(writeEnable),
    .ALUEnable(ALUEnable), .ALUOp(ALUOp), .jumpControl(jumpControl), .ZF(ZF), .CF(CF), .PCLoad(PCload),
    .state_value(state), .regLoad(regLoad), .Clock(Clock), .jumpActivate(jumpActivate));
  Multiplexer #(.width(16), .enable("false")) multiplexer_7 (
    .in0(demultiplexer_3_out0), .in1(bit_extender_1_out), .out(multiplexer_7_out), .sel(ImmEnable));
  Comparator #(.width(16)) comparator_1 (
    .a(demultiplexer_2_out1), .b(demultiplexer_3_out1), .eq(comparator_1_eq), .lt(comparator_1_lt));  // open: gt
  Demultiplexer #(.width(16), .enable("false")) demultiplexer_4 (
    .out0(demultiplexer_4_out0), .out1(demultiplexer_4_out1), .in(demultiplexer_2_out0), .sel(regStore));
  Demultiplexer #(.width(16), .enable("false")) demultiplexer_5 (
    .out0(demultiplexer_5_out0), .in(multiplexer_7_out), .sel(regStore));  // open: out1
  Demultiplexer #(.width(16), .enable("false")) demultiplexer_6 (
    .out1(demultiplexer_6_out1), .in(demultiplexer_4_out0), .sel(ALUEnable));  // open: out0
  Demultiplexer #(.width(16), .enable("false")) demultiplexer_7 (
    .out1(demultiplexer_7_out1), .in(demultiplexer_5_out0), .sel(ALUEnable));  // open: out0
  Multiplexer #(.width(16), .enable("false")) multiplexer_8 (
    .in0(demultiplexer_10_out1), .in1(ram_1_data), .out(multiplexer_8_out), .sel(regLoad));
  assign bit_extender_2_out = {{4{1'b0}}, {Reg1, Reg2}};  // Bit_Extender bit_extender_2
  Demultiplexer #(.enable("false")) demultiplexer_8 (
    .out1(demultiplexer_8_out1), .in(comparator_1_eq), .sel(writeFlag));  // open: out0
  Demultiplexer #(.enable("false")) demultiplexer_9 (
    .out1(demultiplexer_9_out1), .in(comparator_1_lt), .sel(writeFlag));  // open: out0
  ALU alu_1 (
    .Data_input_1(demultiplexer_6_out1), .Data_input_2(demultiplexer_7_out1),
    .Result_of_operation(alu_1_result_of_operation), .ALU_Control(ALUOp));
  Demultiplexer #(.width(16), .enable("false")) demultiplexer_10 (
    .out1(demultiplexer_10_out1), .in(TempReg_q), .sel(writeEnable));  // open: out0
  Register #(.width(1)) u_ZF (.D(demultiplexer_8_out1), .en(compare), .Q(ZF), .clk(Clock));  // open: clr
  Register #(.width(1)) u_CF (.D(demultiplexer_9_out1), .en(compare), .Q(CF), .clk(Clock));  // open: clr
  Register #(.width(16)) TempReg (
    .D(alu_1_result_of_operation), .en(ALUEnable), .Q(TempReg_q), .clk(Clock));  // open: clr
  RAM #(.addrWidth(12), .dataWidth(16), .bus("separate")) ram_1 (
    .addr(bit_extender_2_out), .din(demultiplexer_4_out1), .data(ram_1_data), .str(regStore),
    .sel(DataEnable), .clk(Clock), .ld(regLoad));  // open: clr

  // Notes on the sheet:
  //   contents of rom_1 (hex, n*v repeats v):
  //   1014 b000 a100 b101 210 b202 4010 5ffe
endmodule

module Control_Unit (
  input  Clock,
  input  [3:0] opcode,
  input  ZF,
  input  CF,
  output [3:0] state_value,
  output jumpActivate,
  output PCRead,
  output PCSelect,
  output writeEnable,
  output compare,
  output ImmEnable,
  output regStore,
  output ALUEnable,
  output ALUOp,
  output jumpControl,
  output DataEnable,
  output writeFlag,
  output regLoad,
  output PCLoad
);

  wire ADD, ADDI, ALUEnable1, ALUEnable2, ALUEnable3, ALUEnable4, AND, and_2_out, and_35_out, and_49_out,
       and_50_out, and_75_out, ANDI, CMP, DataEnable2, JA, JAE, JB, JBE, JE, JUMP, jumpActivate1,
       jumpActivate2, jumpActivate3, jumpActivate4, jumpActivate5, jumpActivate6, jumpControl1, jumpControl2,
       jumpControl3, jumpControl4, jumpControl5, jumpControl6, jumpDetect, LD, not_1_out, not_2_out,
       not_3_out, not_4_out, not_5_out, or_1_out, PCLoad1, PCLoad2, PCLoad3, PCLoad4, PCLoad5, PCLoad12,
       PCLoad13, PCRead1, PCRead2, PCRead3, PCRead4, PCRead5, PCRead6, PCRead7, PCRead8, PCRead9, PCRead10,
       PCRead11, PCRead12, PCRead13, PCSelect1, PCSelect2, PCSelect3, PCSelect4, PCSelect5, resetState,
       resetState1, resetState2, resetState3, resetState4, resetState5, resetState6, resetState7,
       resetState8, resetState9, resetState10, resetState11, resetState12, resetState13, ST, State_1,
       State_2, State_3, State_4, State_5, State_6, State_7, State_8, State_9, State_10, State_11, State_12,
       State_13, State_14, State_15, State_16, writeEnable1, writeEnable2, writeEnable3, writeEnable4,
       writeEnable5, xor_1_out;

  Counter #(.width(4), .max('hf)) counter_1 (
    .Q(state_value), .clk(Clock), .clr(resetState));  // open: load, D, count, carry
  Decoder #(.select(4), .enable("false")) decoder_1 (
    .out0(ADD), .out1(ADDI), .out2(AND), .out3(ANDI), .out4(CMP), .out5(JE), .out6(JA), .out7(JB),
    .out8(JBE), .out9(JAE), .out10(LD), .out11(ST), .out12(JUMP), .sel(opcode));  // open: out13, out14, out15
  Decoder #(.select(4), .enable("false")) decoder_2 (
    .out0(State_1), .out1(State_2), .out2(State_3), .out3(State_4), .out4(State_5), .out5(State_6),
    .out6(State_7), .out7(State_8), .out8(State_9), .out9(State_10), .out10(State_11), .out11(State_12),
    .out12(State_13), .out13(State_14), .out14(State_15), .out15(State_16), .sel(state_value));
  and and_1 (writeEnable2, State_4, ADDI);
  and and_2 (and_2_out, State_1, ADD);
  and and_3 (writeEnable1, State_5, ADD);
  // AND_Gate and_4 has open pins: in0=State_1, in1=ADDI, out=open
  and and_5 (PCRead1, State_2, ADD);
  and and_6 (PCRead2, State_2, ADDI);
  and and_7 (PCLoad1, State_6, ADD);
  and and_8 (PCLoad2, State_5, ADDI);
  and and_9 (ALUEnable2, State_3, ADDI);
  // AND_Gate and_10 has open pins: in0=State_3, in1=ADD, out=open
  and and_11 (resetState2, State_6, ADDI);
  or or_1 (or_1_out, JE, JA, JB, JBE, JAE, JUMP);
  and and_12 (resetState1, State_7, ADD);
  Register #(.width(1)) register_1 (.D(or_1_out), .Q(jumpDetect), .clk(Clock));  // open: en, clr
  and and_13 (ALUEnable1, State_4, ADD);
  or or_2 (jumpActivate, jumpActivate1, jumpActivate2, jumpActivate3, jumpActivate4, jumpActivate5, jumpActivate6);
  // AND_Gate and_14 has open pins: in0=State_1, in1=AND, out=open
  and and_15 (writeEnable3, State_4, AND);
  // AND_Gate and_16 has open pins: in0=State_1, in1=ANDI, out=open
  and and_17 (writeEnable4, State_4, ANDI);
  and and_18 (PCRead4, State_2, ANDI);
  and and_19 (PCRead3, State_2, AND);
  and and_20 (PCLoad4, State_5, ANDI);
  and and_21 (PCLoad3, State_5, AND);
  and and_22 (ALUEnable3, State_3, AND);
  and and_23 (ALUEnable4, State_3, ANDI);
  and and_24 (resetState3, State_6, AND);
  and and_25 (resetState4, State_6, ANDI);
  // AND_Gate and_26 has open pins: in0=State_1, in1=CMP, out=open
  and and_27 (PCLoad5, State_4, CMP);
  // AND_Gate and_28 has open pins: in0=State_1, in1=JE, out=open
  or or_3 (PCRead, PCRead1, PCRead2, PCRead3, PCRead4, PCRead5, PCRead6, PCRead7, PCRead8, PCRead9, PCRead10, PCRead11, PCRead12, PCRead13);
  and and_29 (jumpActivate1, State_4, JE);
  and and_30 (PCRead5, State_2, CMP);
  and and_31 (PCRead6, State_2, JE);
  and and_32 (resetState5, State_5, CMP);
  and and_33 (compare, State_3, CMP);
  and and_34 (PCSelect1, State_3, JE);
  and and_35 (and_35_out, ZF, not_1_out);
  not not_1 (not_1_out, CF);
  and and_36 (resetState6, State_5, JE);
  and and_37 (jumpControl1, PCSelect1, and_35_out);
  or or_4 (PCSelect, PCSelect1, PCSelect2, PCSelect3, PCSelect4, PCSelect5, jumpControl6);
  // AND_Gate and_38 has open pins: in0=State_1, in1=JA, out=open
  // AND_Gate and_39 has open pins: in0=State_1, in1=JB, out=open
  and and_40 (jumpActivate3, State_4, JB);
  and and_41 (jumpActivate2, State_4, JA);
  and and_42 (PCRead7, State_2, JA);
  and and_43 (PCRead8, State_2, JB);
  and and_44 (resetState8, State_5, JB);
  or or_5 (writeEnable, writeEnable1, writeEnable2, writeEnable3, writeEnable4, writeEnable5, 1'b0);
  and and_45 (PCSelect2, State_3, JA);
  not not_2 (not_2_out, ZF);
  not not_3 (not_3_out, CF);
  and and_46 (resetState7, State_5, JA);
  and and_47 (PCSelect3, State_3, JB);
  not not_4 (not_4_out, ZF);
  and and_48 (jumpControl2, PCSelect2, and_49_out);
  and and_49 (and_49_out, not_2_out, not_3_out);
  and and_50 (and_50_out, not_4_out, CF);
  and and_51 (jumpControl3, PCSelect3, and_50_out);
  or or_6 (ImmEnable, ALUEnable2, ALUEnable4);
  // AND_Gate and_52 has open pins: in0=State_1, in1=JAE, out=open
  and and_53 (jumpActivate4, State_4, JAE);
  // AND_Gate and_54 has open pins: in0=State_1, in1=JBE, out=open
  and and_55 (jumpActivate5, State_4, JBE);
  or or_7 (regStore, compare, DataEnable2);
  and and_56 (PCRead9, State_2, JAE);
  and and_57 (PCRead10, State_2, JBE);
  or or_8 (ALUEnable, ALUEnable1, ALUEnable2, ALUEnable3, ALUEnable4);
  and and_58 (resetState9, State_5, JAE);
  and and_59 (resetState10, State_5, JBE);
  and and_60 (PCSelect4, State_3, JAE);
  not not_5 (not_5_out, CF);
  and and_61 (PCSelect5, State_3, JBE);
  and and_62 (jumpControl4, PCSelect4, not_5_out);
  and and_63 (jumpControl5, PCSelect5, xor_1_out);
  xor xor_1 (xor_1_out, CF, ZF);
  or or_9 (ALUOp, ALUEnable3, ALUEnable4);
  // AND_Gate and_64 has open pins: in0=State_1, in1=JUMP, out=open
  and and_65 (jumpActivate6, State_4, JUMP);
  // AND_Gate and_66 has open pins: in0=State_1, in1=LD, out=open
  and and_67 (writeEnable5, State_4, LD);
  or or_10 (DataEnable, regLoad, DataEnable2);
  and and_68 (PCRead11, State_2, JUMP);
  and and_69 (resetState11, State_5, JUMP);
  and and_70 (PCRead12, State_2, LD);
  and and_71 (PCLoad12, State_5, LD);
  or or_11 (jumpControl, jumpControl1, jumpControl2, jumpControl3, jumpControl4, jumpControl5, jumpControl6);
  and and_72 (jumpControl6, State_3, JUMP);
  and and_73 (regLoad, State_3, LD);
  and and_74 (resetState12, State_6, LD);
  and and_75 (and_75_out, State_1, ST);
  and and_76 (PCLoad13, State_4, ST);
  and and_77 (PCRead13, State_2, ST);
  or or_12 (PCLoad, PCLoad1, PCLoad2, PCLoad3, PCLoad4, PCLoad5, jumpActivate1, jumpActivate2, jumpActivate3, jumpActivate4, jumpActivate5, jumpActivate6, PCLoad12, PCLoad13);
  and and_78 (resetState13, State_5, ST);
  and and_79 (DataEnable2, State_3, ST);
  or or_13 (resetState, resetState1, resetState2, resetState3, resetState4, resetState5, resetState6, resetState7, resetState8, resetState9, resetState1, resetState1, resetState12, resetState13);

  assign writeFlag = compare;

  // Other names for the same wires on the sheet: ALUOp1 = ALUEnable3; DataEnable1 = regLoad; ImmEnable1 = ALUEnable2;
  //   ALUOp2 = ALUEnable4; ImmEnable2 = ALUEnable4; PCLoad6 = jumpActivate1; PCLoad7 = jumpActivate2;
  //   PCLoad8 = jumpActivate3; PCLoad9 = jumpActivate4; PCLoad10 = jumpActivate5; PCLoad11 = jumpActivate6;
  //   PCSelect6 = jumpControl6; regStore1 = compare; regStore2 = DataEnable2

  // Notes on the sheet:
  //   ADD
  //   ADDI
  //   AND
  //   ANDI
  //   CMP
  //   JE
  //   JA
  //   JB
  //   JAE
  //   JBE
  //   JUMP
  //   LD
  //   ST
endmodule

module ALU (
  input  [15:0] Data_input_1,
  input  [15:0] Data_input_2,
  input  ALU_Control,
  output [15:0] Result_of_operation
);

  wire [15:0] adder_1_out, and_1_out;

  Adder #(.width(16)) adder_1 (.a(Data_input_1), .b(Data_input_2), .out(adder_1_out));  // open: cin, cout
  assign and_1_out = Data_input_2 & Data_input_1;  // AND_Gate and_1, 16 bits wide
  Multiplexer #(.width(16), .enable("false")) multiplexer_1 (
    .in0(adder_1_out), .in1(and_1_out), .out(Result_of_operation), .sel(ALU_Control));
endmodule

module Register_File (
  input  [3:0] read_register1,
  input  [3:0] write_source__register,
  input  [3:0] read_register_2,
  input  [15:0] write_data,
  input  Clock,
  input  write_enable,
  output [15:0] register_1_data,
  output [15:0] register_2_data
);

  wire and_1_out, and_2_out, and_3_out, and_4_out, and_5_out, and_6_out, and_7_out, and_8_out, and_9_out,
       and_10_out, and_11_out, and_12_out, and_13_out, and_14_out, and_15_out, and_16_out, decoder_1_out0,
       decoder_1_out1, decoder_1_out2, decoder_1_out3, decoder_1_out4, decoder_1_out5, decoder_1_out6,
       decoder_1_out7, decoder_1_out8, decoder_1_out9, decoder_1_out10, decoder_1_out11, decoder_1_out12,
       decoder_1_out13, decoder_1_out14, decoder_1_out15;
  wire [15:0] register_1_q, register_2_q, register_3_q, register_4_q, register_5_q, register_6_q,
       register_7_q, register_8_q, register_9_q, register_10_q, register_11_q, register_12_q, register_13_q,
       register_14_q, register_15_q, register_16_q;

  Decoder #(.select(4), .enable("false")) decoder_1 (
    .out0(decoder_1_out0), .out1(decoder_1_out1), .out2(decoder_1_out2), .out3(decoder_1_out3),
    .out4(decoder_1_out4), .out5(decoder_1_out5), .out6(decoder_1_out6), .out7(decoder_1_out7),
    .out8(decoder_1_out8), .out9(decoder_1_out9), .out10(decoder_1_out10), .out11(decoder_1_out11),
    .out12(decoder_1_out12), .out13(decoder_1_out13), .out14(decoder_1_out14), .out15(decoder_1_out15),
    .sel(write_source__register));
  and and_1 (and_1_out, decoder_1_out0, write_enable);
  and and_2 (and_2_out, decoder_1_out1, write_enable);
  and and_3 (and_3_out, decoder_1_out2, write_enable);
  and and_4 (and_4_out, decoder_1_out3, write_enable);
  and and_5 (and_5_out, decoder_1_out4, write_enable);
  and and_6 (and_6_out, decoder_1_out5, write_enable);
  and and_7 (and_7_out, decoder_1_out6, write_enable);
  and and_8 (and_8_out, decoder_1_out7, write_enable);
  Register #(.width(16)) register_1 (.D(write_data), .en(and_1_out), .Q(register_1_q), .clk(Clock));  // open: clr
  Register #(.width(16)) register_2 (.D(write_data), .en(and_2_out), .Q(register_2_q), .clk(Clock));  // open: clr
  Register #(.width(16)) register_3 (.D(write_data), .en(and_3_out), .Q(register_3_q), .clk(Clock));  // open: clr
  Register #(.width(16)) register_4 (.D(write_data), .en(and_4_out), .Q(register_4_q), .clk(Clock));  // open: clr
  Register #(.width(16)) register_5 (.D(write_data), .en(and_5_out), .Q(register_5_q), .clk(Clock));  // open: clr
  Register #(.width(16)) register_6 (.D(write_data), .en(and_6_out), .Q(register_6_q), .clk(Clock));  // open: clr
  Register #(.width(16)) register_7 (.D(write_data), .en(and_7_out), .Q(register_7_q), .clk(Clock));  // open: clr
  Register #(.width(16)) register_8 (.D(write_data), .en(and_8_out), .Q(register_8_q), .clk(Clock));  // open: clr
  and and_9 (and_9_out, decoder_1_out8, write_enable);
  and and_10 (and_10_out, decoder_1_out9, write_enable);
  and and_11 (and_11_out, decoder_1_out10, write_enable);
  and and_12 (and_12_out, decoder_1_out11, write_enable);
  and and_13 (and_13_out, decoder_1_out12, write_enable);
  and and_14 (and_14_out, decoder_1_out13, write_enable);
  and and_15 (and_15_out, decoder_1_out14, write_enable);
  and and_16 (and_16_out, decoder_1_out15, write_enable);
  Register #(.width(16)) register_9 (.D(write_data), .en(and_9_out), .Q(register_9_q), .clk(Clock));  // open: clr
  Register #(.width(16)) register_10 (.D(write_data), .en(and_10_out), .Q(register_10_q), .clk(Clock));  // open: clr
  Register #(.width(16)) register_11 (.D(write_data), .en(and_11_out), .Q(register_11_q), .clk(Clock));  // open: clr
  Register #(.width(16)) register_12 (.D(write_data), .en(and_12_out), .Q(register_12_q), .clk(Clock));  // open: clr
  Register #(.width(16)) register_13 (.D(write_data), .en(and_13_out), .Q(register_13_q), .clk(Clock));  // open: clr
  Register #(.width(16)) register_14 (.D(write_data), .en(and_14_out), .Q(register_14_q), .clk(Clock));  // open: clr
  Register #(.width(16)) register_15 (.D(write_data), .en(and_15_out), .Q(register_15_q), .clk(Clock));  // open: clr
  Register #(.width(16)) register_16 (.D(write_data), .en(and_16_out), .Q(register_16_q), .clk(Clock));  // open: clr
  Multiplexer #(.select(4), .width(16), .enable("false")) multiplexer_1 (
    .in0(register_1_q), .in1(register_2_q), .in2(register_3_q), .in3(register_4_q), .in4(register_5_q),
    .in5(register_6_q), .in6(register_7_q), .in7(register_8_q), .in8(register_9_q), .in9(register_10_q),
    .in10(register_11_q), .in11(register_12_q), .in12(register_13_q), .in13(register_14_q),
    .in14(register_15_q), .in15(register_16_q), .out(register_1_data), .sel(read_register1));
  Multiplexer #(.select(4), .width(16), .enable("false")) multiplexer_2 (
    .in0(register_1_q), .in1(register_2_q), .in2(register_3_q), .in3(register_4_q), .in4(register_5_q),
    .in5(register_6_q), .in6(register_7_q), .in7(register_8_q), .in8(register_9_q), .in9(register_10_q),
    .in10(register_11_q), .in11(register_12_q), .in12(register_13_q), .in13(register_14_q),
    .in14(register_15_q), .in15(register_16_q), .out(register_2_data), .sel(read_register_2));
endmodule
